# Fritzing sketch main (saved by Fritzing 0.9.6b)
breadboards: 1

parts:
  D1 = LED_BARGRAPH_10 [package=led_bargaph_10]
  R1 = Resistor [tolerance=±5% power=0.25 resistance=220 package=THT]
  R2 = Resistor [tolerance=±5% power=0.25 resistance=220 package=THT]
  R3 = Resistor [tolerance=±5% power=0.25 resistance=220 package=THT]
  R4 = Resistor [tolerance=±5% power=0.25 resistance=220 package=THT]
  R5 = Resistor [tolerance=±5% power=0.25 resistance=220 package=THT]
  PIC_16F877A1 = PIC 16F877A [package=THT]

nets:
  N1: D1.A_A, R2.Pin_0
  N2: D1.B_A, R3.Pin_0
  N3: D1.C_A, R4.Pin_0
  N4: D1.D_A, R5.Pin_0
  N5: D1.E_A, R1.Pin_0
  N6: D1.E_C, PIC_16F877A1.RB4
  N7: D1.D_C, PIC_16F877A1.RB3
  N8: D1.C_C, PIC_16F877A1.RB2
  N9: D1.B_C, PIC_16F877A1.RB1
  N10: D1.A_C, PIC_16F877A1.RB0/INT
  N11: R1.Pin_1, R2.Pin_1, R3.Pin_1, R4.Pin_1, R5.Pin_1, PIC_16F877A1.VSS#30
